// Logisim project pierre-feuille-ciseau.circ as structural Verilog: 1 circuit, main circuit main
module main (
  input  a,
  input  b,
  input  c,
  input  d,
  output L1,
  output L2
);

  wire AD_L1_3_out, AND_L1_1_out, AND_L1_2_out, AND_L1_4_out, AND_L2_1_out, AND_L2_2_out, AND_L2_3_out,
       AND_L2_4_out, not_1_out, not_2_out, not_3_out, not_4_out, not_5_out, not_6_out, not_7_out, not_8_out;

  and AND_L1_1 (AND_L1_1_out, a, c, d);
  and AND_L1_2 (AND_L1_2_out, a, not_1_out, c);
  not not_1 (not_1_out, b);
  not not_2 (not_2_out, a);
  and AD_L1_3 (AD_L1_3_out, not_2_out, b, not_3_out, c);
  not not_3 (not_3_out, d);
  and AND_L1_4 (AND_L1_4_out, b, not_4_out, d);
  not not_4 (not_4_out, c);
  not not_5 (not_5_out, a);
  and AND_L2_1 (AND_L2_1_out, not_5_out, b, d);
  and AND_L2_2 (AND_L2_2_out, a, c, not_6_out);
  not not_6 (not_6_out, d);
  and AND_L2_3 (AND_L2_3_out, b, c, d);
  not not_7 (not_7_out, b);
  and AND_L2_4 (AND_L2_4_out, a, not_7_out, not_8_out, d);
  not not_8 (not_8_out, c);
  or OR_L1 (L1, AND_L1_1_out, AND_L1_2_out, AD_L1_3_out, AND_L1_4_out);
  or OR_L2 (L2, AND_L2_1_out, AND_L2_2_out, AND_L2_3_out, AND_L2_4_out);
endmodule
