// Logisim project Labo_VGA_25MHz_Basys3_etu.circ as structural Verilog: 11 circuits, main circuit VGA_ctrl
module VGA_ctrl (
  input  [11:0] pixel_in,
  input  clk,
  input  reset,
  output [11:0] pixel,
  output hsync,
  output vsync,
  output [9:0] H_out,
  output [8:0] V_out,
  output frame
);

  wire blank, comparator_1_gt, comparator_2_gt, comparator_3_gt, comparator_4_gt, d_ff_2_p1,
       multiplexer_1_p4, not_1_out, undriven, undriven_3;
  wire [1:0] subtractor_1_out;
  wire [9:0] undriven_4;
  wire [9:9] subtractor_2_out;
  wire [11:0] undriven_2;

  // Counter #(.width(12), .max('hc6a)) h_counter: pin names not known; wires that end beside it: reset, reset, 1'b0, 1'b1
  // Counter #(.width(10), .max('h20d)) v_counter: pin names not known; wires that end beside it: reset, reset, reset, reset, reset, 1'b0, 1'b1
  Comparator #(.width(12), .mode("unsigned")) comparator_1 (
    .a(undriven_2), .b(12'haee), .gt(comparator_1_gt));  // open: eq, lt
  not not_1 (not_1_out, comparator_1_gt);
  D_Flip_Flop d_ff_1 (.en(clk));  // open: clk, D, Q, Qn, preset, reset
  // Probe on undriven_4
  Comparator #(.width(10), .mode("unsigned")) comparator_2 (
    .a(undriven_4), .b(10'h20b), .gt(comparator_2_gt));  // open: eq, lt
  // D_Flip_Flop d_ff_2: pin names not known; wires that end beside it: d_ff_2_p1, clk
  not not_2 (d_ff_2_p1, comparator_2_gt);
  Subtractor #(.width(12)) subtractor_1 (
    .a(undriven_2), .b(12'h40), .out({H_out, subtractor_1_out}));  // open: bin, bout
  Subtractor #(.width(10)) subtractor_2 (
    .a(undriven_4), .b(10'h11), .out({subtractor_2_out[9], V_out}));  // open: bin, bout
  and and_1 (frame, undriven_3, undriven);
  // Multiplexer #(.width(12)) multiplexer_1: pin names not known; wires that end beside it: pixel_in, {12{1'b0}}, blank, multiplexer_1_p4, 1'b1, clk
  Comparator #(.width(12), .mode("unsigned")) comparator_3 (
    .a({H_out, subtractor_1_out}), .b(12'h9ff), .gt(comparator_3_gt));  // open: eq, lt
  Comparator #(.width(10), .mode("unsigned")) comparator_4 (
    .a({subtractor_2_out[9], V_out}), .b(10'h1df), .gt(comparator_4_gt));  // open: eq, lt
  // Register #(.width(12)) register_1: pin names not known; wires that end beside it: multiplexer_1_p4, multiplexer_1_p4, 1'b1
  or or_1 (blank, comparator_3_gt, comparator_4_gt);

  // Other names for the same wires on the sheet: pixel_int[11:0] = pixel_in

  // Notes on the sheet:
  //   vsync: pull=up
  //   hsync: pull=up
  //   pixel: pull=up
  //   Ne pas modifier ce circuit!!!!!
  //   Ne pas modifier ce circuit!!!!!
  //   Contrôle VGA 640 x 480 @ 60 Hz
  //   Ne pas modifier ce circuit!!!!!
endmodule

module Exercise (
  input  [9:0] H_in,
  input  [9:0] V_in,
  input  [7:0] SW,
  output [11:0] Pixel
);

  Drapeau_VD drapeau_vd_1 (.H_in(H_in), .V_in(V_in), .SW(SW), .Pixel(Pixel));
  Drapeau_FR drapeau_fr_1 (.H_in(H_in), .V_in(V_in), .SW(SW), .Pixel(Pixel));
  Drapeau_CH drapeau_ch_1 (.H_in(H_in), .V_in(V_in), .SW(SW), .Pixel(Pixel));

  // Notes on the sheet:
  //   Coordonnée horizontale, valeurs entre 0 et 639
  //   Coordonnée verticale, valeurs entre 0 et 479
endmodule

module Image_Gen (
  input  clk,
  input  reset,
  input  [7:0] SW,
  output [11:0] pixel,
  output hsync,
  output vsync
);

  wire VGA_p4, VGA_p5;
  wire [11:0] Drapeaux_pixel;

  // VGA_ctrl VGA: pin names not known; wires that end beside it: pixel, hsync, vsync, VGA_p4, VGA_p5
  Exercise Drapeaux (.Pixel(Drapeaux_pixel));  // open: H_in, V_in, SW

  // Notes on the sheet:
  //   vsync: pull=up
  //   hsync: pull=up
  //   pixel: pull=up
  //   Ne pas modifier ce circuit!!!!!
  //   Ne pas modifier ce circuit!!!!!
endmodule

module SIM_VGA_ctrl (
  input  rst,
  input  clk,
  output [4:0] H_out,
  output [4:0] V_out,
  output frame,
  output blank
);

  wire undriven, undriven_2;

  // Counter #(.width(5), .max('h1f)) h_counter: pin names not known; wires that end beside it: rst, rst, 1'b0, 1'b1
  // Counter #(.width(5), .max('h1f)) v_counter: pin names not known; wires that end beside it: rst, rst, 1'b0, 1'b1
  Comparator #(.width(5), .mode("unsigned")) comparator_1 (.a(V_out), .b(5'b10111), .gt(blank));  // open: eq, lt
  and and_1 (frame, undriven_2, undriven);

  // Notes on the sheet:
  //   Ne pas modifier ce circuit!!!!!
endmodule

module SIM_image_Gen (
  input  rst,
  input  clk,
  input  [7:0] Switch,
  output [4:0] H_count,
  output [4:0] V_count,
  output [2:0] Pixel
);

  wire sim_vga_ctrl_1_p3;
  wire [4:0] sim_vscaler_1_out_2;
  wire [5:0] sim_hscaler_1_out_2;
  wire [11:0] exercise_1_pixel;

  // SIM_VGA_ctrl sim_vga_ctrl_1: pin names not known; wires that end beside it: H_count, V_count, sim_vga_ctrl_1_p3
  SIM_hscaler sim_hscaler_1 (.out_2(sim_hscaler_1_out_2));  // open: in_1
  SIM_vscaler sim_vscaler_1 (.out_2(sim_vscaler_1_out_2));  // open: in_1
  Exercise exercise_1 (.Pixel(exercise_1_pixel));  // open: H_in, V_in, SW
  Multiplexer #(.width(3)) multiplexer_1 (
    .in0({exercise_1_pixel[11], exercise_1_pixel[7], exercise_1_pixel[3]}), .in1(3'b000), .out(Pixel),
    .sel(sim_vga_ctrl_1_p3));  // open: en

  // Notes on the sheet:
  //   Ne pas modifier ce circuit!!!!!
  //   Ne pas modifier ce circuit!!!!!
endmodule

module SIM_console (
  input  reset,
  input  [7:0] Switch
);

  wire clk_out;
  wire [2:0] sim_image_gen_1_pixel;
  wire [4:0] sim_image_gen_1_h_count, sim_image_gen_1_v_count;

  Clock clk (.out(clk_out));
  SIM_image_Gen sim_image_gen_1 (
    .rst(reset), .clk(clk_out), .Switch(Switch), .H_count(sim_image_gen_1_h_count),
    .V_count(sim_image_gen_1_v_count), .Pixel(sim_image_gen_1_pixel));

  // Notes on the sheet:
  //   Ne pas modifier ce circuit!!!!!
  //   Ne pas modifier ce circuit!!!!!
endmodule

module SIM_hscaler (
  input  [4:0] in_1,
  output [5:0] out_2
);

  wire [6:0] bit_extender_1_out, multiplier_1_out;
  wire [6:6] divider_1_out;

  assign bit_extender_1_out = {{2{1'b0}}, in_1};  // Bit_Extender bit_extender_1
  Multiplier #(.width(7)) multiplier_1 (
    .a(bit_extender_1_out), .b(7'b0000100), .out(multiplier_1_out));  // open: cin, cout
  Divider #(.width(7)) divider_1 (
    .a(multiplier_1_out), .b(7'b0000011), .out({divider_1_out[6], out_2}));  // open: upper, rem

  // Notes on the sheet:
  //   Ne pas modifier ce circuit!!!!!
endmodule

module SIM_vscaler (
  input  [4:0] in_1,
  output [4:0] out_2
);

  wire [6:0] bit_extender_1_out, multiplier_1_out;
  wire [6:5] divider_1_out;

  assign bit_extender_1_out = {{2{1'b0}}, in_1};  // Bit_Extender bit_extender_1
  Multiplier #(.width(7)) multiplier_1 (
    .a(bit_extender_1_out), .b(7'b0000100), .out(multiplier_1_out));  // open: cin, cout
  Divider #(.width(7)) divider_1 (
    .a(multiplier_1_out), .b(7'b0000011), .out({divider_1_out, out_2}));  // open: upper, rem

  // Notes on the sheet:
  //   Ne pas modifier ce circuit!!!!!
endmodule

module Drapeau_FR (
  input  [9:0] H_in,
  input  [9:0] V_in,
  input  [7:0] SW,
  output [11:0] Pixel
);

  wire [1:0] comparator_1_lt;

  Comparator #(.width(10), .mode("unsigned")) comparator_1 (
    .a(H_in), .b(10'hd5), .lt(comparator_1_lt[0]));  // open: gt, eq
  Comparator #(.width(10), .mode("unsigned")) comparator_2 (
    .a(H_in), .b(10'h1aa), .gt(comparator_1_lt[1]));  // open: eq, lt
  Multiplexer #(.select(2), .width(12)) multiplexer_1 (
    .in0({12{1'b1}}), .in1(12'hf), .in2(12'hf00), .out(Pixel), .sel(comparator_1_lt));  // open: in3, en

  // Notes on the sheet:
  //   Coordonnée horizontale, valeurs entre 0 et 639
  //   Coordonnée verticale, valeurs entre 0 et 479
endmodule

module Drapeau_VD (
  input  [9:0] H_in,
  input  [9:0] V_in,
  input  [7:0] SW,
  output [11:0] Pixel
);

  wire comparator_1_gt;

  Comparator #(.width(10), .mode("unsigned")) comparator_1 (
    .a(V_in), .b(10'hef), .gt(comparator_1_gt));  // open: eq, lt
  Multiplexer #(.width(12)) multiplexer_1 (
    .in0({12{1'b1}}), .in1(12'hf0), .out(Pixel), .sel(comparator_1_gt));  // open: en

  // Notes on the sheet:
  //   Coordonnée horizontale, valeurs entre 0 et 639
  //   Coordonnée verticale, valeurs entre 0 et 479
endmodule

module Drapeau_CH (
  input  [9:0] H_in,
  input  [9:0] V_in,
  input  [7:0] SW,
  output [11:0] Pixel
);

  wire and_1_out, comparator_1_lt, comparator_2_lt;

  Comparator #(.width(10), .mode("unsigned")) comparator_1 (
    .a(H_in), .b(10'h13f), .lt(comparator_1_lt));  // open: gt, eq
  Comparator #(.width(10), .mode("unsigned")) comparator_2 (
    .a(V_in), .b(10'h13f), .lt(comparator_2_lt));  // open: gt, eq
  and and_1 (and_1_out, comparator_1_lt, comparator_2_lt);
  Multiplexer #(.width(12)) multiplexer_1 (
    .in0({12{1'b1}}), .in1(12'hf00), .out(Pixel), .sel(and_1_out), .en(and_1_out));

  // Notes on the sheet:
  //   Coordonnée horizontale, valeurs entre 0 et 639
  //   Coordonnée verticale, valeurs entre 0 et 479
endmodule
